// Logisim project lab3.circ as structural Verilog: 4 circuits, main circuit main
module main (
  input  A0,
  input  A1,
  input  A2,
  input  A3,
  input  A4,
  input  A5,
  input  A6,
  input  A7,
  input  B0,
  input  B1,
  input  B2,
  input  B3,
  input  B4,
  input  B5,
  input  B6,
  input  B7,
  output S2,
  output S3,
  output S4,
  output S5,
  output S6,
  output S1,
  output S0,
  output S7,
  output overflow
);

  wire fulladder_1_cout, fulladder_2_cout, fulladder_3_cout, fulladder_4_cout, fulladder_5_cout,
       fulladder_6_cout, fulladder_7_cout;

  FullAdder fulladder_1 (.A(A0), .B(B0), .Cin(1'b0), .Sum(S0), .Cout(fulladder_1_cout));
  FullAdder fulladder_2 (.A(A1), .B(B1), .Cin(fulladder_1_cout), .Sum(S1), .Cout(fulladder_2_cout));
  FullAdder fulladder_3 (.A(A2), .B(B2), .Cin(fulladder_2_cout), .Sum(S2), .Cout(fulladder_3_cout));
  FullAdder fulladder_4 (.A(A3), .B(B3), .Cin(fulladder_3_cout), .Sum(S3), .Cout(fulladder_4_cout));
  FullAdder fulladder_5 (.A(A4), .B(B4), .Cin(fulladder_4_cout), .Sum(S4), .Cout(fulladder_5_cout));
  FullAdder fulladder_6 (.A(A5), .B(B5), .Cin(fulladder_5_cout), .Sum(S5), .Cout(fulladder_6_cout));
  FullAdder fulladder_7 (.A(A6), .B(B6), .Cin(fulladder_6_cout), .Sum(S6), .Cout(fulladder_7_cout));
  FullAdder fulladder_8 (.A(A7), .B(B7), .Cin(fulladder_7_cout), .Sum(S7), .Cout(overflow));
endmodule

module FullAdder (
  input  A,
  input  B,
  input  Cin,
  output Sum,
  output Cout
);

  wire not_1_out, not_2_out, not_3_out, not_4_out, not_5_out, not_6_out, OR1_out, OR2_out, OR3_out, OR4_out,
       OR5_out, OR6_out, OR7_out;

  or OR1 (OR1_out, Cin, B, A);
  not not_1 (not_1_out, Cin);
  not not_2 (not_2_out, B);
  or OR2 (OR2_out, not_1_out, not_2_out, A);
  and AND1 (Sum, OR1_out, OR2_out, OR3_out, OR4_out);
  not not_3 (not_3_out, Cin);
  not not_4 (not_4_out, A);
  or OR3 (OR3_out, not_3_out, B, not_4_out);
  not not_5 (not_5_out, B);
  not not_6 (not_6_out, A);
  or OR4 (OR4_out, Cin, not_5_out, not_6_out);
  or OR5 (OR5_out, B, A);
  or OR6 (OR6_out, Cin, A);
  and AND2 (Cout, OR5_out, OR6_out, OR7_out);
  or OR7 (OR7_out, Cin, B);
endmodule

module Excess3Plus1 (
  input  X8,
  input  X4,
  input  X2,
  input  X1,
  output Y1,
  output Y2,
  output Carry,
  output Y4,
  output Y8
);

  wire and_1_out, and_2_out, and_3_out, and_4_out, and_5_out, and_6_out, and_7_out, and_8_out, and_9_out,
       and_10_out, and_11_out, and_12_out, and_13_out, and_14_out, and_15_out, and_16_out, and_17_out,
       and_18_out, not_1_out, not_2_out, not_3_out, not_4_out, not_5_out, not_6_out, not_7_out, not_8_out,
       not_9_out, not_10_out, not_11_out, not_12_out, not_13_out, not_14_out, not_15_out, not_16_out,
       not_17_out, not_18_out, not_19_out, not_20_out, not_21_out, not_22_out, not_23_out, not_24_out,
       not_25_out, not_26_out, not_27_out, not_28_out, not_29_out, not_30_out, not_31_out, not_32_out,
       not_33_out, not_34_out, not_35_out, not_36_out, not_37_out, not_38_out, not_39_out;

  not not_1 (not_1_out, X1);
  not not_2 (not_2_out, X4);
  and and_1 (and_1_out, not_1_out, X2, not_2_out, X8);
  not not_3 (not_3_out, X1);
  not not_4 (not_4_out, X8);
  and and_2 (and_2_out, not_3_out, X2, X4, not_4_out);
  or or_1 (Y1, and_1_out, and_2_out, and_3_out, and_4_out);
  not not_5 (not_5_out, X1);
  not not_6 (not_6_out, X2);
  not not_7 (not_7_out, X8);
  and and_3 (and_3_out, not_5_out, not_6_out, X4, not_7_out);
  not not_8 (not_8_out, X1);
  not not_9 (not_9_out, X2);
  not not_10 (not_10_out, X4);
  and and_4 (and_4_out, not_8_out, not_9_out, not_10_out, X8);
  not not_11 (not_11_out, X1);
  not not_12 (not_12_out, X4);
  and and_5 (and_5_out, not_11_out, X2, not_12_out, X8);
  not not_13 (not_13_out, X2);
  not not_14 (not_14_out, X8);
  and and_6 (and_6_out, X1, not_13_out, X4, not_14_out);
  not not_15 (not_15_out, X1);
  not not_16 (not_16_out, X8);
  and and_7 (and_7_out, not_15_out, X2, X4, not_16_out);
  or or_2 (Y2, and_5_out, and_6_out, and_7_out, and_8_out);
  not not_17 (not_17_out, X2);
  not not_18 (not_18_out, X4);
  and and_8 (and_8_out, X1, not_17_out, not_18_out, X8);
  and and_9 (and_9_out, X1, X2, not_21_out, not_22_out);
  not not_19 (not_19_out, X1);
  not not_20 (not_20_out, X2);
  not not_21 (not_21_out, X4);
  not not_22 (not_22_out, X8);
  and and_10 (and_10_out, not_19_out, not_20_out, X4, not_23_out);
  not not_23 (not_23_out, X8);
  not not_24 (not_24_out, X2);
  and and_11 (and_11_out, X1, not_24_out, X4, not_25_out);
  or or_3 (Y4, and_9_out, and_10_out, and_11_out, and_12_out, and_13_out);
  not not_25 (not_25_out, X8);
  not not_26 (not_26_out, X1);
  and and_12 (and_12_out, not_26_out, X2, X4, not_27_out);
  not not_27 (not_27_out, X8);
  not not_28 (not_28_out, X4);
  and and_13 (and_13_out, X1, X2, not_28_out, X8);
  not not_29 (not_29_out, X1);
  not not_30 (not_30_out, X2);
  not not_31 (not_31_out, X4);
  and and_14 (and_14_out, not_29_out, not_30_out, not_31_out, X8);
  not not_32 (not_32_out, X2);
  not not_33 (not_33_out, X4);
  and and_15 (and_15_out, X1, not_32_out, not_33_out, X8);
  not not_34 (not_34_out, X1);
  not not_35 (not_35_out, X4);
  and and_16 (and_16_out, not_34_out, X2, not_35_out, X8);
  or or_4 (Y8, and_14_out, and_15_out, and_16_out, and_17_out, and_18_out);
  and and_17 (and_17_out, X1, X2, X4, not_36_out);
  not not_36 (not_36_out, X8);
  not not_37 (not_37_out, X4);
  and and_18 (and_18_out, X1, X2, not_37_out, X8);
  not not_38 (not_38_out, X1);
  not not_39 (not_39_out, X2);
  and and_19 (Carry, not_38_out, not_39_out, X4, X8);
endmodule

module UpCounter8 (
  output Q0,
  output Q1,
  output Q2
);

  wire and_1_out, clock_1_out;

  Clock clock_1 (.out(clock_1_out));
  T_Flip_Flop t_ff_1 (.T(1'b1), .clk(clock_1_out), .Q(Q0), .reset(1'b0), .preset(1'b0));  // open: Qn
  T_Flip_Flop t_ff_2 (.T(Q0), .clk(clock_1_out), .Q(Q1), .reset(1'b0), .preset(1'b0));  // open: Qn
  and and_1 (and_1_out, Q0, Q1);
  T_Flip_Flop t_ff_3 (.T(and_1_out), .clk(clock_1_out), .Q(Q2), .reset(1'b0), .preset(1'b0));  // open: Qn
endmodule
